# Fritzing sketch simon (saved by Fritzing 0.9.3b)
breadboards: 1

parts:
  R1 = Resistor [tolerance=±10% resistance=0.22 package=THT]
  LED1 = LED - 5mm [color="Red (633nm)" package="5 mm [THT]"]
  LED2 = LED - 5mm [color="Green (560nm)" package="5 mm [THT]"]
  LED3 = LED - 5mm [color="Yellow (592nm)" package="5 mm [THT]"]
  Componente1 = Arduino Uno (Rev3)
  R2 = Resistor [tolerance=±10% resistance=0.22 package=THT]
  R3 = Resistor [tolerance=±10% resistance=0.22 package=THT]
  S1 = Pushbutton [package="[THT]"]
  J1 = Piezo Speaker
  R4 = Rotary Potentiometer (Small) [maximum_resistance=100kΩ package=THT]
  R5 = Resistor [tolerance=±10% resistance=12k package=THT]
  R6 = Resistor [tolerance=±10% resistance=12k package=THT]
  S2 = Pushbutton [package="[THT]"]
  R7 = Resistor [tolerance=±10% resistance=12k package=THT]
  S3 = Pushbutton [package="[THT]"]

nets:
  N1: R1.Pin_0, LED3.anode
  N2: R1.Pin_1, Componente1.D9_PWM
  N3: LED1.cathode, LED2.cathode, LED3.cathode, Componente1.GND, J1.pin1, R4.leg2
  N4: LED1.anode, R2.Pin_0
  N5: LED2.anode, R3.Pin_0
  N6: Componente1.A0, Componente1.A1, R5.Pin_0, R6.Pin_0, R6.Pin_1, S2.Pin_1, S2.Pin_2, R7.Pin_0, R7.Pin_1, S3.Pin_1, S3.Pin_2
  N7: Componente1.A2, Componente1.5V, S1.Pin_1, S1.Pin_2, R5.Pin_1
  N8: Componente1.A5/SCL, R4.wiper
  N9: Componente1.D8, R2.Pin_1
  N10: Componente1.D10_PWM/SS, R3.Pin_1
  N11: Componente1.D2, J1.pin2
